// Logisim project adders.circ as structural Verilog: 1 circuit, main circuit main
module main (
  input  A,
  input  B,
  input  A_2,
  input  B_2,
  input  Cin,
  output out_6,
  output out_7,
  output sum,
  output Cout
);

  wire and_2_out, and_3_out, xor_2_out;

  xor xor_1 (out_6, A, B);
  and and_1 (out_7, A, B);
  xor xor_2 (xor_2_out, A_2, B_2);
  and and_2 (and_2_out, B_2, A_2);
  and and_3 (and_3_out, Cin, xor_2_out);
  xor xor_3 (sum, xor_2_out, Cin);
  or or_1 (Cout, and_3_out, and_2_out);
endmodule
