// Logisim project addersUsingnNAND.circ as structural Verilog: 1 circuit, main circuit main
module main (
  input  A,
  input  B,
  input  A_2,
  input  B_2,
  input  C,
  output sum,
  output carry,
  output sum_2,
  output Cout
);

  wire nand_1_out, nand_2_out, nand_3_out, nand_4_out, nand_5_out, nand_6_out, nand_7_out, nand_8_out,
       nand_11_out, nand_12_out;

  nand nand_1 (nand_1_out, A_2, B_2);
  nand nand_2 (nand_2_out, A_2, nand_1_out);
  nand nand_3 (nand_3_out, nand_1_out, B_2);
  nand nand_4 (nand_4_out, nand_2_out, nand_3_out);
  nand nand_5 (nand_5_out, nand_4_out, C);
  nand nand_6 (nand_6_out, nand_4_out, nand_5_out);
  nand nand_7 (nand_7_out, nand_5_out, C);
  nand nand_8 (nand_8_out, A, B);
  nand nand_9 (sum_2, nand_6_out, nand_7_out);
  nand nand_10 (Cout, nand_1_out, nand_5_out);
  nand nand_11 (nand_11_out, A, nand_8_out);
  nand nand_12 (nand_12_out, nand_8_out, B);
  nand nand_13 (carry, nand_8_out, nand_8_out);
  nand nand_14 (sum, nand_11_out, nand_12_out);
endmodule
