// Logisim project 4bitAdder.circ as structural Verilog: 1 circuit, main circuit main
module main (
  input  C0in,
  input  A0,
  input  B0,
  input  C0in_2,
  input  A0_2,
  input  B0_2,
  input  A1,
  input  B1,
  input  A2,
  input  A1_2,
  input  B2,
  input  B1_2,
  input  A3,
  input  B3,
  input  A2_2,
  input  B2_2,
  input  A3_2,
  input  B3_2,
  output S0,
  output S0_2,
  output S1,
  output S2,
  output S1_2,
  output S3,
  output Cout,
  output S2_2,
  output S3_2,
  output Cout_2
);

  wire adder_1_cout, adder_2_cout, adder_3_cout, and_1_out, and_2_out, and_3_out, and_4_out, and_5_out,
       and_6_out, and_7_out, and_8_out, or_1_out, or_2_out, or_3_out, xor_1_out, xor_2_out, xor_3_out,
       xor_4_out;

  Adder #(.width(1)) adder_1 (.a(A0_2), .b(B0_2), .out(S0_2), .cin(C0in), .cout(adder_1_cout));
  Adder #(.width(1)) adder_2 (.a(A1), .b(B1), .out(S1), .cin(adder_1_cout), .cout(adder_2_cout));
  Adder #(.width(1)) adder_3 (.a(A2), .b(B2), .out(S2), .cin(adder_2_cout), .cout(adder_3_cout));
  Adder #(.width(1)) adder_4 (.a(A3), .b(B3), .out(S3), .cin(adder_3_cout), .cout(Cout));
  xor xor_1 (xor_1_out, A0, B0);
  and and_1 (and_1_out, B0, A0);
  xor xor_2 (xor_2_out, A1_2, B1_2);
  and and_2 (and_2_out, B1_2, A1_2);
  xor xor_3 (xor_3_out, A2_2, B2_2);
  and and_3 (and_3_out, B2_2, A2_2);
  xor xor_4 (xor_4_out, A3_2, B3_2);
  and and_4 (and_4_out, B3_2, A3_2);
  xor xor_5 (S0, xor_1_out, C0in_2);
  and and_5 (and_5_out, xor_1_out, C0in_2);
  xor xor_6 (S1_2, xor_2_out, or_1_out);
  and and_6 (and_6_out, xor_2_out, or_1_out);
  and and_7 (and_7_out, xor_3_out, or_2_out);
  and and_8 (and_8_out, xor_4_out, or_3_out);
  xor xor_7 (S2_2, xor_3_out, or_2_out);
  xor xor_8 (S3_2, xor_4_out, or_3_out);
  or or_1 (or_1_out, and_5_out, and_1_out);
  or or_2 (or_2_out, and_6_out, and_2_out);
  or or_3 (or_3_out, and_7_out, and_3_out);
  or or_4 (Cout_2, and_8_out, and_4_out);
endmodule
