// Logisim project mux2x1and4x1.circ as structural Verilog: 1 circuit, main circuit main
module main (
  input  in_1,
  input  in_2,
  input  in_3,
  input  in_4,
  input  in_5,
  input  in_6,
  input  in_7,
  input  s,
  input  in_9,
  input  in_10,
  input  in_11,
  input  in_12,
  input  in_13,
  input  in_14,
  input  in_15,
  input  in_16,
  input  in_17,
  input  in_18,
  input  in_19,
  input  in_20,
  input  in_21,
  input  s0,
  input  s1,
  output out_24,
  output out_25,
  output out_26,
  output out_27
);

  wire and_1_out, and_2_out, and_3_out, and_4_out, and_5_out, and_6_out, multiplexer_1_out,
       multiplexer_2_out, multiplexer_3_out, multiplexer_4_out, not_1_out, not_2_out, not_3_out;

  not not_1 (not_1_out, s);
  not not_2 (not_2_out, s0);
  not not_3 (not_3_out, s1);
  and and_1 (and_1_out, not_1_out, in_2);
  and and_2 (and_2_out, in_4, s);
  and and_3 (and_3_out, in_15, not_2_out, not_3_out);
  and and_4 (and_4_out, in_18, s1, not_2_out);
  and and_5 (and_5_out, in_20, s0, not_3_out);
  and and_6 (and_6_out, s0, s1, in_21);
  or or_1 (out_24, and_1_out, and_2_out);
  or or_2 (out_27, and_3_out, and_4_out, and_5_out, and_6_out);
  Multiplexer multiplexer_1 (.in0(in_1), .in1(in_3), .out(multiplexer_1_out), .sel(in_5));  // open: en
  Multiplexer multiplexer_2 (.in0(in_6), .in1(in_7), .out(multiplexer_2_out), .sel(in_10));  // open: en
  Multiplexer multiplexer_3 (.in0(in_11), .in1(in_12), .out(multiplexer_3_out), .sel(in_13));  // open: en
  Multiplexer multiplexer_4 (.in0(in_14), .in1(in_16), .out(multiplexer_4_out), .sel(in_19));  // open: en
  Multiplexer multiplexer_5 (.in0(multiplexer_1_out), .in1(multiplexer_2_out), .out(out_25), .sel(in_9));  // open: en
  Multiplexer multiplexer_6 (.in0(multiplexer_3_out), .in1(multiplexer_4_out), .out(out_26), .sel(in_17));  // open: en
endmodule
