// Logisim project encoder8x3.circ as structural Verilog: 1 circuit, main circuit main
module main (
  input  Y0,
  input  Y1,
  input  Y2,
  input  Y3,
  input  Y4,
  input  Y5,
  input  Y6,
  input  Y7,
  output A2,
  output A1,
  output A0
);

  or or_1 (A2, Y4, Y5, Y6, Y7);
  or or_2 (A0, Y1, Y3, Y5, Y7);
  or or_3 (A1, Y2, Y3, Y6, Y7);
endmodule
